// Logisim project ex1.circ as structural Verilog: 5 circuits, main circuit NAND1
module NAND1 (
  input  A,
  input  B,
  output RESULT
);


  // Notes on the sheet:
  //   METTRE VOTRE CIRCUIT ICI
endmodule

module NOR1 (
  input  A,
  input  B,
  output RESULT
);


  // Notes on the sheet:
  //   METTRE VOTRE CIRCUIT ICI
endmodule

module XOR1 (
  input  A,
  input  B,
  output RESULT
);


  // Notes on the sheet:
  //   METTRE VOTRE CIRCUIT ICI
endmodule

module MUX2 (
  input  A,
  input  B,
  input  Sel,
  output RESULT
);


  // Notes on the sheet:
  //   METTRE VOTRE CIRCUIT ICI
endmodule

module MUX4 (
  input  A,
  input  B,
  input  C,
  input  D,
  input  Sel1,
  input  Sel2,
  output RESULT
);


  // Notes on the sheet:
  //   METTRE VOTRE CIRCUIT ICI
endmodule
