// Logisim project ex2.circ as structural Verilog: 1 circuit, main circuit AddMachine
module AddMachine (
  output [7:0] ADD_OUT,
  output [7:0] REG_OUT
);


  // Notes on the sheet:
  //   METTRE VOTRE CIRCUIT ICI
endmodule
